// Logisim project MIPS_LastVers.circ as structural Verilog: 13 circuits, main circuit ALU
module main (
  input  in_1
);

  wire ALUSrc, ALUSrc_C, ALUSrc_ID, Branch_C, Branch_ID, clk, controlunit_1_bnq, EM_reg_write, equal, FwA,
       FwB, id_ex_1_mem_write_out, ID_EX_MemRead, IE_reg_write, JR, jump, jump_C, MemRead, MemRead_C,
       MemRead_ID, MemWrite, MemWrite_C, MemWrite_ID, Mux_Stall, or_1_out, PCSrc, reg_write, reg_write_C,
       reg_write_ID, Stall, zero;
  wire [1:0] emux_slct_1_muxa_slct, emux_slct_1_muxb_slct, ex_mem_1_mem_to_reg_out,
       forwarding_unit_1_forwarda, forwarding_unit_1_forwardb, id_ex_1_mem_to_reg_out, MemToReg, MemToReg_C,
       MemToReg_ID, Priority_select, RegDst, RegDst_C, RegDst_ID;
  wire [2:0] alu_control, controlunit_1_alu_control, EM_write_reg, id_ex_1_rs_out, id_ex_1_rt_out, IE_Rd,
       IE_write_reg, write_reg;
  wire [8:0] bit_extender_1_out, bit_extender_4_out;
  wire [15:0] adder_1_out, adder_2_out, bit_extender_2_out, EM_Result, equal_muxs_1_rd1_out,
       equal_muxs_1_rd2_out, ex_mem_1_pc_adder_out, ex_mem_1_read_data2_out, Extended_IR,
       id_ex_1_immediate_out, id_ex_1_pc_adder_out, id_ex_1_reg_data_1_out, id_ex_1_reg_data_2_out,
       if_id_1_pc_adder_out, IM, IR, mem_wb_1_alu_result_out, mem_wb_1_pc_adder_out, mem_wb_1_read_data_out,
       multiplexer_1_out, multiplexer_2_out, multiplexer_3_out, multiplexer_4_out, multiplexer_8_out,
       multiplexer_9_out, multiplexer_11_out, PC_q, ram_1_dout, RD1, RD2, ReadData1, ReadData2, Result,
       WriteData;

  Multiplexer #(.select(2), .width(16)) multiplexer_1 (
    .in0(adder_1_out), .in1(multiplexer_4_out), .in2(bit_extender_2_out), .in3(RD1), .out(multiplexer_1_out),
    .sel(Priority_select));
  Multiplexer #(.width(16)) multiplexer_2 (.in0(multiplexer_1_out), .in1(RD1), .out(multiplexer_2_out), .sel(JR));
  Register #(.width(16)) PC (.D(multiplexer_2_out), .en(Stall), .clk(clk), .Q(PC_q), .clr(in_1));
  Priority_Encoder #(.select(2)) priority_encoder_1 (
    .in0(1'b1), .in1(PCSrc), .in2(jump), .in3(JR), .out(Priority_select));  // open: gs, en_out, en_in
  Clock clock_1 (.out(clk));
  Adder #(.width(16)) adder_1 (.a(16'h1), .b(PC_q), .out(adder_1_out));  // open: cin, cout
  ROM #(.addrWidth(9), .dataWidth(16)) rom_1 (.addr(bit_extender_1_out), .data(IM));
  Bit_Extender #(.in_width(16), .out_width(9)) bit_extender_1 (.in(PC_q), .out(bit_extender_1_out));
  not not_1 (Stall, Mux_Stall);
  Adder #(.width(16)) adder_2 (.a(adder_1_out), .b(Extended_IR), .out(adder_2_out));  // open: cin, cout
  or or_1 (or_1_out, jump_C, PCSrc);
  Multiplexer #(.width(16)) multiplexer_3 (.in0(IM), .in1({16{1'b0}}), .out(multiplexer_3_out), .sel(or_1_out));
  IF_ID if_id_1 (
    .IR_In(multiplexer_3_out), .PC_Adder_In(adder_1_out), .Enable(Stall), .Clk(clk), .CLR(1'b0), .IR_Out(IR),
    .PC_Adder_Out(if_id_1_pc_adder_out));
  Multiplexer #(.width(16)) multiplexer_4 (.in0(adder_1_out), .in1(adder_2_out), .out(multiplexer_4_out), .sel(PCSrc));
  Multiplexer #(.width(10)) multiplexer_5 (
    .in0({jump_C, Branch_C, MemToReg_C, MemRead_C, MemWrite_C, RegDst_C, ALUSrc_C, reg_write_C}),
    .in1({10{1'b0}}),
    .out({jump, Branch_ID, MemToReg_ID, MemRead_ID, MemWrite_ID, RegDst_ID, ALUSrc_ID, reg_write_ID}),
    .sel(Mux_Stall));
  ControlUnit controlunit_1 (
    .OpCode(IR[15:12]), .funct(IR[2:0]), .reg_write(reg_write_C), .alu_control(controlunit_1_alu_control),
    .ALUSrc(ALUSrc_C), .RegDst(RegDst_C), .MemWrite(MemWrite_C), .MemRead(MemRead_C), .MemToReg(MemToReg_C),
    .branch(Branch_C), .jump(jump_C), .BNQ(controlunit_1_bnq), .JR(JR));
  registers registers_1 (
    .read_reg1(IR[11:9]), .read_reg2(IR[8:6]), .write_reg(write_reg), .write_data(WriteData),
    .reg_write(reg_write), .clock(clk), .ReadData1(ReadData1), .ReadData2(ReadData2));
  assign bit_extender_2_out = {{4{IR[11]}}, IR[11:0]};  // Bit_Extender bit_extender_2
  assign Extended_IR = {{10{IR[5]}}, IR[5:0]};  // Bit_Extender bit_extender_3
  Equal_Muxs equal_muxs_1 (
    .ReadData1(RD1), .ReadData2(RD2), .ALUResult(Result), .EX_MEM_R(EM_Result),
    .MuxA_Slct(emux_slct_1_muxa_slct), .MuxB_Slct(emux_slct_1_muxb_slct), .RD1_out(equal_muxs_1_rd1_out),
    .RD2_out(equal_muxs_1_rd2_out));
  Multiplexer #(.width(16)) multiplexer_6 (.in0(ReadData1), .in1(WriteData), .out(RD1), .sel(FwA));
  logical_decision logical_decision_1 (.Branch(Branch_ID), .Zero(equal), .BNQ(controlunit_1_bnq), .PCSrc(PCSrc));
  emux_slct emux_slct_1 (
    .IF_ID_Rt(IR[8:6]), .IF_ID_Rs(IR[11:9]), .ID_EX_Rd(IE_Rd), .ID_EX_RegWrite(IE_reg_write),
    .EX_MEM_Rd(EM_write_reg), .EX_MEM_RegWrite(EM_reg_write), .MuxA_Slct(emux_slct_1_muxa_slct),
    .MuxB_Slct(emux_slct_1_muxb_slct));
  Multiplexer #(.width(16)) multiplexer_7 (.in0(ReadData2), .in1(WriteData), .out(RD2), .sel(FwB));
  Comparator #(.width(16)) comparator_1 (
    .a(equal_muxs_1_rd1_out), .b(equal_muxs_1_rd2_out), .eq(equal));  // open: gt, lt
  Hazard_Unit hazard_unit_1 (
    .ID_EX_MemRead(ID_EX_MemRead), .WB_WriteReg(write_reg), .WB_RegWrite(reg_write),
    .ID_EX_Rt(id_ex_1_rt_out), .IF_ID_RS(IR[11:9]), .IF_ID_RT(IR[8:6]), .Opcode_In(IR[15:12]),
    .ID_EX_WriteReg(IE_write_reg), .ID_EX_RegWrite(IE_reg_write), .EX_MEM_WriteReg(EM_write_reg),
    .EX_MEM_RegWrite(EM_reg_write), .FW_B_ID(FwB), .FW_A_ID(FwA), .Stall(Mux_Stall));
  ID_EX id_ex_1 (
    .PC_adder_in(if_id_1_pc_adder_out), .Reg_Write_In(reg_write_ID),
    .ALU_Control_In(controlunit_1_alu_control), .ALU_Src_In(ALUSrc_ID), .Reg_Dst_In(RegDst_ID),
    .Mem_Write_In(MemWrite_ID), .Mem_Read_In(MemRead_ID), .Mem_To_Reg_In(MemToReg_ID), .Rs_In(IR[11:9]),
    .Rt_In(IR[8:6]), .Rd_In(IR[5:3]), .Reg_Data_1_In(RD1), .Reg_Data_2_In(RD2), .Immediate_In(Extended_IR),
    .Enable(1'b1), .Clk(clk), .CLR(1'b0), .PC_adder_out(id_ex_1_pc_adder_out), .Reg_Write_Out(IE_reg_write),
    .ALU_Control_Out(alu_control), .ALU_Src_Out(ALUSrc), .Reg_Dst_Out(RegDst),
    .Mem_Write_Out(id_ex_1_mem_write_out), .Mem_Read_Out(ID_EX_MemRead),
    .Mem_To_Reg_Out(id_ex_1_mem_to_reg_out), .Reg_Data_1_Out(id_ex_1_reg_data_1_out),
    .Reg_Data_2_Out(id_ex_1_reg_data_2_out), .Rs_Out(id_ex_1_rs_out), .Rt_Out(id_ex_1_rt_out),
    .Rd_Out(IE_Rd), .Immediate_Out(id_ex_1_immediate_out));
  Multiplexer #(.width(16)) multiplexer_8 (
    .in0(multiplexer_11_out), .in1(id_ex_1_immediate_out), .out(multiplexer_8_out), .sel(ALUSrc));
  Multiplexer #(.select(2), .width(16)) multiplexer_9 (
    .in0(id_ex_1_reg_data_1_out), .in1(WriteData), .in2(EM_Result), .out(multiplexer_9_out),
    .sel(forwarding_unit_1_forwarda));  // open: in3
  Multiplexer #(.select(2), .width(3)) multiplexer_10 (
    .in0(IE_Rd), .in1(id_ex_1_rt_out), .in2(3'b111), .out(IE_write_reg), .sel(RegDst));  // open: in3
  ALU alu_1 (
    .alu_control(alu_control), .inputA(multiplexer_9_out), .inputB(multiplexer_8_out), .Result(Result),
    .zeroflag(zero));  // open: in_2
  Multiplexer #(.select(2), .width(16)) multiplexer_11 (
    .in0(id_ex_1_reg_data_2_out), .in1(WriteData), .in2(EM_Result), .out(multiplexer_11_out),
    .sel(forwarding_unit_1_forwardb));  // open: in3
  Forwarding_Unit forwarding_unit_1 (
    .ID_EX_Rs(id_ex_1_rs_out), .ID_EX_Rt(id_ex_1_rt_out), .EX_MEM_write_reg(EM_write_reg),
    .MEM_WB_write_reg(write_reg), .EX_MEM_reg_write(EM_reg_write), .MEM_WB_reg_write(reg_write),
    .ForwardB(forwarding_unit_1_forwardb), .ForwardA(forwarding_unit_1_forwarda));
  EX_MEM ex_mem_1 (
    .Read_Data2_In(id_ex_1_reg_data_2_out), .Write_Reg_In(IE_write_reg), .PC_adder_in(id_ex_1_pc_adder_out),
    .Alu_Result_In(Result), .Reg_Write_In(IE_reg_write), .Mem_Write_In(id_ex_1_mem_write_out),
    .Mem_Read_In(ID_EX_MemRead), .Mem_To_Reg_In(id_ex_1_mem_to_reg_out), .Enable(1'b1), .Clk(clk),
    .CLR(1'b0), .PC_adder_out(ex_mem_1_pc_adder_out), .Alu_Result_Out(EM_Result),
    .Reg_Write_Out(EM_reg_write), .Mem_Write_Out(MemWrite), .Mem_Read_Out(MemRead),
    .Mem_To_Reg_Out(ex_mem_1_mem_to_reg_out), .Read_Data2_Out(ex_mem_1_read_data2_out),
    .Write_Reg_Out(EM_write_reg));
  RAM #(.addrWidth(9), .asyncread("true"), .dataWidth(16)) ram_1 (
    .addr(bit_extender_4_out), .we(MemWrite), .oe(MemRead), .clk(clk), .din(ex_mem_1_read_data2_out),
    .dout(ram_1_dout));
  Bit_Extender #(.in_width(16), .out_width(9)) bit_extender_4 (.in(EM_Result), .out(bit_extender_4_out));
  MEM_WB mem_wb_1 (
    .Reg_Write_In(EM_reg_write), .Mem_To_Reg_In(ex_mem_1_mem_to_reg_out), .Alu_Result_In(EM_Result),
    .Read_Data_In(ram_1_dout), .Write_Reg_In(EM_write_reg), .PC_adder_in(ex_mem_1_pc_adder_out),
    .Enable(1'b1), .Clk(clk), .Reg_Write_Out(reg_write), .Mem_To_Reg_Out(MemToReg),
    .Alu_Result_Out(mem_wb_1_alu_result_out), .Read_Data_Out(mem_wb_1_read_data_out),
    .Write_Reg_Out(write_reg), .PC_adder_out(mem_wb_1_pc_adder_out));
  Multiplexer #(.select(2), .width(16)) multiplexer_12 (
    .in0(mem_wb_1_alu_result_out), .in1(mem_wb_1_read_data_out), .in2(mem_wb_1_pc_adder_out),
    .out(WriteData), .sel(MemToReg));  // open: in3

  // Other names for the same wires on the sheet: opcode[3:0] = IR[15:12]

  // Notes on the sheet:
  //   contents of rom_1 (hex, n*v repeats v):
  //   3045 3085 6281 30c9 9004 a008 9006 0 3243 e05
  //   IF/ID
  //   R type
  //   2.Rs          11-9
  //   3.Rt           8-6
  //   4.Rd          5-3
  //   5.Funct     0-2
  //   1.Opcode 15-12
  //   J type
  //   I type
  //   ID/EX
  //   rs
  //   rd
  //   rt
  //   EX/MEM
  //   MEM/WB
endmodule

module ALU (
  input  [2:0] alu_control,
  input  [15:0] in_2,
  input  [15:0] inputA,
  input  [15:0] inputB,
  output [15:0] Result,
  output zeroflag
);

  wire [15:0] adder_1_out, and_1_out, bit_extender_1_out, or_1_out, subtractor_1_out;

  Adder #(.width(16)) adder_1 (.a(inputB), .b(inputA), .out(adder_1_out));  // open: cin, cout
  Subtractor #(.width(16)) subtractor_1 (.a(inputA), .b(inputB), .out(subtractor_1_out));  // open: bin, bout
  assign and_1_out = inputB & inputA;  // AND_Gate and_1, 16 bits wide
  assign or_1_out = inputB | inputA;  // OR_Gate or_1, 16 bits wide
  Multiplexer #(.select(3), .width(16)) multiplexer_1 (
    .in0(adder_1_out), .in1(subtractor_1_out), .in2(and_1_out), .in3(or_1_out), .in4(bit_extender_1_out),
    .out(Result), .sel(alu_control));  // open: in5, in6, in7
  assign bit_extender_1_out = {{15{1'b0}}, subtractor_1_out[15]};  // Bit_Extender bit_extender_1
  Comparator #(.width(16)) comparator_1 (.a(Result), .b(in_2), .eq(zeroflag));  // open: gt, lt
endmodule

module registers (
  input  [2:0] read_reg1,
  input  [2:0] read_reg2,
  input  [2:0] write_reg,
  input  [15:0] write_data,
  input  reg_write,
  input  clock,
  output [15:0] ReadData1,
  output [15:0] ReadData2
);

  wire decoder_1_out0, decoder_1_out1, decoder_1_out2, decoder_1_out3, decoder_1_out4, decoder_1_out5,
       decoder_1_out6, decoder_1_out7;
  wire [15:0] register_1_q, register_2_q, register_3_q, register_4_q, register_5_q, register_6_q,
       register_7_q, register_8_q;

  Register #(.width(16)) register_1 (.D(write_data), .en(decoder_1_out0), .clk(clock), .Q(register_1_q));  // open: clr
  Register #(.width(16)) register_2 (.D(write_data), .en(decoder_1_out1), .clk(clock), .Q(register_2_q));  // open: clr
  Register #(.width(16)) register_3 (.D(write_data), .en(decoder_1_out2), .clk(clock), .Q(register_3_q));  // open: clr
  Register #(.width(16)) register_4 (.D(write_data), .en(decoder_1_out3), .clk(clock), .Q(register_4_q));  // open: clr
  Register #(.width(16)) register_5 (.D(write_data), .en(decoder_1_out4), .clk(clock), .Q(register_5_q));  // open: clr
  Register #(.width(16)) register_6 (.D(write_data), .en(decoder_1_out5), .clk(clock), .Q(register_6_q));  // open: clr
  Register #(.width(16)) register_7 (.D(write_data), .en(decoder_1_out6), .clk(clock), .Q(register_7_q));  // open: clr
  Register #(.width(16)) register_8 (.D(write_data), .en(decoder_1_out7), .clk(clock), .Q(register_8_q));  // open: clr
  Multiplexer #(.select(3), .width(16)) multiplexer_1 (
    .in0({16{1'b0}}), .in1(register_2_q), .in2(register_3_q), .in3(register_4_q), .in4(register_5_q),
    .in5(register_6_q), .in6(register_7_q), .in7(register_8_q), .out(ReadData1), .sel(read_reg1));
  Multiplexer #(.select(3), .width(16)) multiplexer_2 (
    .in0({16{1'b0}}), .in1(register_2_q), .in2(register_3_q), .in3(register_4_q), .in4(register_5_q),
    .in5(register_6_q), .in6(register_7_q), .in7(register_8_q), .out(ReadData2), .sel(read_reg2));
  Decoder #(.select(3)) decoder_1 (
    .out0(decoder_1_out0), .out1(decoder_1_out1), .out2(decoder_1_out2), .out3(decoder_1_out3),
    .out4(decoder_1_out4), .out5(decoder_1_out5), .out6(decoder_1_out6), .out7(decoder_1_out7),
    .sel(write_reg), .en(reg_write));

  // Notes on the sheet:
  //   write_data: initial=0x1234
endmodule

module ControlUnit (
  input  [3:0] OpCode,
  input  [2:0] funct,
  output reg_write,
  output [2:0] alu_control,
  output ALUSrc,
  output [1:0] RegDst,
  output MemWrite,
  output MemRead,
  output [1:0] MemToReg,
  output branch,
  output jump,
  output BNQ,
  output JR
);

  wire ADDI, ANDI, comparator_1_eq, E, J, R_type, SLTI, SUBI;
  wire [0:0] or_5_out;

  Decoder #(.enable("false"), .select(4)) decoder_1 (
    .out0(R_type), .out1(MemRead), .out2(MemWrite), .out3(ADDI), .out4(SUBI), .out5(SLTI), .out6(branch),
    .out7(BNQ), .out8(ANDI), .out9(J), .out10(MemToReg[1]), .out11(E), .out12(E), .out13(E), .out14(E),
    .sel(OpCode));  // open: out15
  Comparator #(.mode("unsigned"), .width(3)) comparator_1 (
    .a(funct), .b(3'b101), .eq(comparator_1_eq));  // open: gt, lt
  or or_1 (reg_write, R_type, MemRead, ADDI, SUBI, SLTI, ANDI, MemToReg[1]);
  or or_2 (ALUSrc, MemRead, MemWrite, ADDI, SUBI, SLTI, ANDI);
  or or_3 (RegDst[0], MemRead, ADDI, SUBI, SLTI, ANDI);
  or or_4 (jump, J, MemToReg[1]);
  and and_1 (JR, comparator_1_eq, R_type);
  or or_5 (or_5_out[0], SUBI, branch, BNQ);
  Multiplexer #(.width(3)) multiplexer_1 (
    .in0({SLTI, ANDI, or_5_out[0]}), .in1(funct), .out(alu_control), .sel(R_type));

  assign MemToReg[0] = MemRead;
  assign RegDst[1] = MemToReg[1];

  // Other names for the same wires on the sheet: BEQ = branch; LW = MemRead; JAL = MemToReg[1]; SW = MemWrite
endmodule

module IF_ID (
  input  [15:0] PC_Adder_In,
  input  [15:0] IR_In,
  input  CLR,
  input  Enable,
  input  Clk,
  output [15:0] PC_Adder_Out,
  output [15:0] IR_Out
);

  Register #(.width(16)) register_1 (.D(PC_Adder_In), .en(Enable), .clk(Clk), .Q(PC_Adder_Out), .clr(CLR));
  Register #(.width(16)) register_2 (.D(IR_In), .en(Enable), .clk(Clk), .Q(IR_Out), .clr(CLR));
endmodule

module ID_EX (
  input  [15:0] PC_adder_in,
  input  Reg_Write_In,
  input  [2:0] ALU_Control_In,
  input  ALU_Src_In,
  input  [1:0] Reg_Dst_In,
  input  Mem_Write_In,
  input  Mem_Read_In,
  input  [1:0] Mem_To_Reg_In,
  input  [15:0] Reg_Data_1_In,
  input  [15:0] Reg_Data_2_In,
  input  [2:0] Rs_In,
  input  [2:0] Rt_In,
  input  [2:0] Rd_In,
  input  [15:0] Immediate_In,
  input  CLR,
  input  Enable,
  input  Clk,
  output [15:0] PC_adder_out,
  output Reg_Write_Out,
  output [2:0] ALU_Control_Out,
  output ALU_Src_Out,
  output [1:0] Reg_Dst_Out,
  output Mem_Write_Out,
  output Mem_Read_Out,
  output [1:0] Mem_To_Reg_Out,
  output [15:0] Reg_Data_1_Out,
  output [15:0] Reg_Data_2_Out,
  output [2:0] Rs_Out,
  output [2:0] Rt_Out,
  output [2:0] Rd_Out,
  output [15:0] Immediate_Out
);

  Register #(.width(16)) register_1 (.D(PC_adder_in), .en(Enable), .Q(PC_adder_out), .clk(Clk), .clr(CLR));
  Register #(.width(1)) register_2 (.D(Reg_Write_In), .en(Enable), .Q(Reg_Write_Out), .clk(Clk), .clr(CLR));
  Register #(.width(3)) register_3 (.D(ALU_Control_In), .en(Enable), .Q(ALU_Control_Out), .clk(Clk), .clr(CLR));
  Register #(.width(1)) register_4 (.D(ALU_Src_In), .en(Enable), .Q(ALU_Src_Out), .clk(Clk), .clr(CLR));
  Register #(.width(2)) register_5 (.D(Reg_Dst_In), .en(Enable), .Q(Reg_Dst_Out), .clk(Clk), .clr(CLR));
  Register #(.width(1)) register_6 (.D(Mem_Write_In), .en(Enable), .Q(Mem_Write_Out), .clk(Clk), .clr(CLR));
  Register #(.width(1)) register_7 (.D(Mem_Read_In), .en(Enable), .Q(Mem_Read_Out), .clk(Clk), .clr(CLR));
  Register #(.width(2)) register_8 (.D(Mem_To_Reg_In), .en(Enable), .Q(Mem_To_Reg_Out), .clk(Clk), .clr(CLR));
  Register #(.width(1)) register_9 (.en(Enable), .clk(Clk), .clr(CLR));  // open: D, Q
  Register #(.width(1)) register_10 (.en(Enable), .clk(Clk), .clr(CLR));  // open: D, Q
  Register #(.width(16)) register_11 (.D(Reg_Data_1_In), .en(Enable), .Q(Reg_Data_1_Out), .clk(Clk), .clr(CLR));
  Register #(.width(16)) register_12 (.D(Reg_Data_2_In), .en(Enable), .Q(Reg_Data_2_Out), .clk(Clk), .clr(CLR));
  Register #(.width(3)) register_13 (.D(Rs_In), .en(Enable), .Q(Rs_Out), .clk(Clk), .clr(CLR));
  Register #(.width(3)) register_14 (.D(Rt_In), .en(Enable), .Q(Rt_Out), .clk(Clk), .clr(CLR));
  Register #(.width(3)) register_15 (.D(Rd_In), .en(Enable), .Q(Rd_Out), .clk(Clk), .clr(CLR));
  Register #(.width(16)) register_16 (.D(Immediate_In), .en(Enable), .Q(Immediate_Out), .clk(Clk), .clr(CLR));
endmodule

module EX_MEM (
  input  [15:0] PC_adder_in,
  input  Reg_Write_In,
  input  Mem_Write_In,
  input  Mem_Read_In,
  input  [1:0] Mem_To_Reg_In,
  input  [15:0] Alu_Result_In,
  input  [15:0] Read_Data2_In,
  input  [2:0] Write_Reg_In,
  input  CLR,
  input  Enable,
  input  Clk,
  output [15:0] PC_adder_out,
  output Reg_Write_Out,
  output Mem_Write_Out,
  output Mem_Read_Out,
  output [1:0] Mem_To_Reg_Out,
  output [15:0] Alu_Result_Out,
  output [15:0] Read_Data2_Out,
  output [2:0] Write_Reg_Out
);

  Register #(.width(16)) register_1 (.D(PC_adder_in), .en(Enable), .clk(Clk), .Q(PC_adder_out), .clr(CLR));
  Register #(.width(1)) register_2 (.D(Reg_Write_In), .en(Enable), .clk(Clk), .Q(Reg_Write_Out), .clr(CLR));
  Register #(.width(1)) register_3 (.D(Mem_Write_In), .en(Enable), .clk(Clk), .Q(Mem_Write_Out), .clr(CLR));
  Register #(.width(1)) register_4 (.D(Mem_Read_In), .en(Enable), .clk(Clk), .Q(Mem_Read_Out), .clr(CLR));
  Register #(.width(2)) register_5 (.D(Mem_To_Reg_In), .en(Enable), .clk(Clk), .Q(Mem_To_Reg_Out), .clr(CLR));
  Register #(.width(1)) register_6 (.en(Enable), .clk(Clk), .clr(CLR));  // open: D, Q
  Register #(.width(1)) register_7 (.en(Enable), .clk(Clk), .clr(CLR));  // open: D, Q
  Register #(.width(16)) register_8 (.D(Alu_Result_In), .en(Enable), .clk(Clk), .Q(Alu_Result_Out), .clr(CLR));
  Register #(.width(1)) register_9 (.en(Enable), .clk(Clk), .clr(CLR));  // open: D, Q
  Register #(.width(16)) register_10 (.D(Read_Data2_In), .en(Enable), .clk(Clk), .Q(Read_Data2_Out), .clr(CLR));
  Register #(.width(3)) register_11 (.D(Write_Reg_In), .en(Enable), .clk(Clk), .Q(Write_Reg_Out), .clr(CLR));
endmodule

module MEM_WB (
  input  [15:0] PC_adder_in,
  input  Reg_Write_In,
  input  [1:0] Mem_To_Reg_In,
  input  [15:0] Alu_Result_In,
  input  [15:0] Read_Data_In,
  input  [2:0] Write_Reg_In,
  input  Enable,
  input  Clk,
  output [15:0] PC_adder_out,
  output Reg_Write_Out,
  output [1:0] Mem_To_Reg_Out,
  output [15:0] Alu_Result_Out,
  output [15:0] Read_Data_Out,
  output [2:0] Write_Reg_Out
);

  Register #(.width(16)) register_1 (.D(PC_adder_in), .en(Enable), .clk(Clk), .Q(PC_adder_out));  // open: clr
  Register #(.width(1)) register_2 (.D(Reg_Write_In), .en(Enable), .clk(Clk), .Q(Reg_Write_Out));  // open: clr
  Register #(.width(2)) register_3 (.D(Mem_To_Reg_In), .en(Enable), .clk(Clk), .Q(Mem_To_Reg_Out));  // open: clr
  Register #(.width(16)) register_4 (.D(Alu_Result_In), .en(Enable), .clk(Clk), .Q(Alu_Result_Out));  // open: clr
  Register #(.width(16)) register_5 (.D(Read_Data_In), .en(Enable), .clk(Clk), .Q(Read_Data_Out));  // open: clr
  Register #(.width(3)) register_6 (.D(Write_Reg_In), .en(Enable), .clk(Clk), .Q(Write_Reg_Out));  // open: clr
endmodule

module logical_decision (
  input  Branch,
  input  Zero,
  input  BNQ,
  output PCSrc
);

  wire and_1_out, and_2_out, not_1_out;

  not not_1 (not_1_out, Zero);
  and and_1 (and_1_out, Branch, Zero);
  and and_2 (and_2_out, not_1_out, BNQ);
  or or_1 (PCSrc, and_1_out, and_2_out);
endmodule

module Forwarding_Unit (
  input  [2:0] ID_EX_Rs,
  input  [2:0] ID_EX_Rt,
  input  [2:0] EX_MEM_write_reg,
  input  [2:0] MEM_WB_write_reg,
  input  EX_MEM_reg_write,
  input  MEM_WB_reg_write,
  output [1:0] ForwardA,
  output [1:0] ForwardB
);

  wire and_3_out, and_4_out, comparator_1_eq, comparator_2_eq, comparator_2_lt, comparator_3_eq,
       comparator_4_eq, comparator_4_lt, comparator_5_eq, comparator_6_eq, comparator_7_eq, comparator_8_eq,
       not_1_out, not_2_out, not_3_out, not_4_out, not_5_out, not_6_out;

  Comparator #(.width(3)) comparator_1 (.a(ID_EX_Rs), .b(EX_MEM_write_reg), .eq(comparator_1_eq));  // open: gt, lt
  Comparator #(.width(3)) comparator_2 (
    .a(EX_MEM_write_reg), .b(3'b000), .eq(comparator_2_eq), .lt(comparator_2_lt));  // open: gt
  Comparator #(.width(3)) comparator_3 (.a(ID_EX_Rt), .b(EX_MEM_write_reg), .eq(comparator_3_eq));  // open: gt, lt
  Comparator #(.width(3)) comparator_4 (
    .a(EX_MEM_write_reg), .b(3'b000), .eq(comparator_4_eq), .lt(comparator_4_lt));  // open: gt
  not not_1 (not_1_out, comparator_2_eq);
  not not_2 (not_2_out, comparator_4_eq);
  and and_1 (ForwardA[1], comparator_1_eq, not_1_out, EX_MEM_reg_write);
  and and_2 (ForwardB[1], comparator_3_eq, not_2_out, EX_MEM_reg_write);
  Comparator #(.width(3)) comparator_5 (.a(ID_EX_Rs), .b(MEM_WB_write_reg), .eq(comparator_5_eq));  // open: gt, lt
  Comparator #(.width(3)) comparator_6 (.a(MEM_WB_write_reg), .b(3'b000), .eq(comparator_6_eq));  // open: gt, lt
  Comparator #(.width(3)) comparator_7 (.a(ID_EX_Rt), .b(MEM_WB_write_reg), .eq(comparator_7_eq));  // open: gt, lt
  Comparator #(.width(3)) comparator_8 (.a(MEM_WB_write_reg), .b(3'b000), .eq(comparator_8_eq));  // open: gt, lt
  not not_3 (not_3_out, comparator_6_eq);
  not not_4 (not_4_out, comparator_8_eq);
  and and_3 (and_3_out, comparator_5_eq, not_3_out, MEM_WB_reg_write);
  and and_4 (and_4_out, comparator_7_eq, not_4_out, MEM_WB_reg_write);
  not not_5 (not_5_out, ForwardA[1]);
  not not_6 (not_6_out, ForwardB[1]);
  and and_5 (ForwardA[0], not_5_out, and_3_out);
  and and_6 (ForwardB[0], not_6_out, and_4_out);

  // Notes on the sheet:
  //   EX_Match_A
  //   EX_Match_B
  //   MEM_Match_B
  //   MEM_Match_A
endmodule

module Hazard_Unit (
  input  ID_EX_MemRead,
  input  [2:0] ID_EX_Rt,
  input  [2:0] IF_ID_RS,
  input  [2:0] IF_ID_RT,
  input  [3:0] Opcode_In,
  input  [2:0] ID_EX_WriteReg,
  input  ID_EX_RegWrite,
  input  [2:0] EX_MEM_WriteReg,
  input  EX_MEM_RegWrite,
  input  [2:0] WB_WriteReg,
  input  WB_RegWrite,
  output Stall,
  output FW_A_ID,
  output FW_B_ID
);

  wire and_1_out, and_2_out, and_3_out, and_4_out, and_5_out, comparator_1_eq, comparator_2_eq,
       comparator_3_eq, comparator_4_eq, comparator_5_eq, comparator_6_eq, comparator_7_eq, comparator_8_eq,
       comparator_9_eq, comparator_10_eq, comparator_11_eq, comparator_12_eq, comparator_13_eq,
       comparator_14_eq, comparator_15_eq, comparator_16_eq, comparator_17_eq, comparator_18_eq, not_1_out,
       not_2_out, or_1_out, or_2_out, or_3_out, or_4_out, or_5_out;

  Comparator #(.mode("unsigned"), .width(3)) comparator_1 (
    .a(ID_EX_Rt), .b(IF_ID_RS), .eq(comparator_1_eq));  // open: gt, lt
  Comparator #(.mode("unsigned"), .width(3)) comparator_2 (
    .a(ID_EX_Rt), .b(IF_ID_RS), .eq(comparator_2_eq));  // open: gt, lt
  Comparator #(.width(4)) comparator_3 (.a(Opcode_In), .b(4'b0010), .eq(comparator_3_eq));  // open: gt, lt
  Comparator #(.width(3)) comparator_4 (.a(IF_ID_RT), .b(ID_EX_WriteReg), .eq(comparator_4_eq));  // open: gt, lt
  Comparator #(.width(4)) comparator_5 (.a(Opcode_In), .b(4'b0010), .eq(comparator_5_eq));  // open: gt, lt
  Comparator #(.width(3)) comparator_6 (.a(IF_ID_RT), .b(EX_MEM_WriteReg), .eq(comparator_6_eq));  // open: gt, lt
  Comparator #(.width(4)) comparator_7 (.a(Opcode_In), .b(4'b0110), .eq(comparator_7_eq));  // open: gt, lt
  Comparator #(.width(4)) comparator_8 (.a(Opcode_In), .b(4'b0111), .eq(comparator_8_eq));  // open: gt, lt
  Comparator #(.width(3)) comparator_9 (.a(IF_ID_RS), .b(ID_EX_WriteReg), .eq(comparator_9_eq));  // open: gt, lt
  Comparator #(.width(3)) comparator_10 (.a(IF_ID_RT), .b(ID_EX_WriteReg), .eq(comparator_10_eq));  // open: gt, lt
  Comparator #(.width(4)) comparator_11 (.a(Opcode_In), .b(4'b0110), .eq(comparator_11_eq));  // open: gt, lt
  Comparator #(.width(4)) comparator_12 (.a(Opcode_In), .b(4'b0111), .eq(comparator_12_eq));  // open: gt, lt
  Comparator #(.width(3)) comparator_13 (.a(IF_ID_RS), .b(EX_MEM_WriteReg), .eq(comparator_13_eq));  // open: gt, lt
  Comparator #(.width(3)) comparator_14 (.a(IF_ID_RT), .b(EX_MEM_WriteReg), .eq(comparator_14_eq));  // open: gt, lt
  Comparator #(.width(3)) comparator_15 (.a(IF_ID_RS), .b(WB_WriteReg), .eq(comparator_15_eq));  // open: gt, lt
  not not_1 (not_1_out, comparator_16_eq);
  Comparator #(.width(1)) comparator_16 (.a(WB_RegWrite), .b(1'b0), .eq(comparator_16_eq));  // open: gt, lt
  Comparator #(.width(3)) comparator_17 (.a(IF_ID_RT), .b(WB_WriteReg), .eq(comparator_17_eq));  // open: gt, lt
  not not_2 (not_2_out, comparator_18_eq);
  Comparator #(.width(1)) comparator_18 (.a(WB_RegWrite), .b(1'b0), .eq(comparator_18_eq));  // open: gt, lt
  or or_1 (or_1_out, comparator_1_eq, comparator_2_eq);
  or or_2 (or_2_out, comparator_7_eq, comparator_8_eq);
  or or_3 (or_3_out, comparator_9_eq, comparator_10_eq);
  or or_4 (or_4_out, comparator_11_eq, comparator_12_eq);
  or or_5 (or_5_out, comparator_13_eq, comparator_14_eq);
  and and_1 (and_1_out, ID_EX_MemRead, or_1_out);
  and and_2 (and_2_out, comparator_3_eq, comparator_4_eq, ID_EX_RegWrite);
  and and_3 (and_3_out, comparator_5_eq, comparator_6_eq, EX_MEM_RegWrite);
  and and_4 (and_4_out, or_2_out, ID_EX_RegWrite, or_3_out);
  and and_5 (and_5_out, or_4_out, EX_MEM_RegWrite, or_5_out);
  and and_6 (FW_A_ID, comparator_15_eq, not_1_out, WB_RegWrite);
  and and_7 (FW_B_ID, comparator_17_eq, not_2_out, WB_RegWrite);
  or or_6 (Stall, and_1_out, and_2_out, and_3_out, and_4_out, and_5_out);

  // Notes on the sheet:
  //   fwdasinyal
  //   fwdbsinyal
endmodule

module Equal_Muxs (
  input  [15:0] ReadData1,
  input  [15:0] ReadData2,
  input  [15:0] ALUResult,
  input  [1:0] MuxA_Slct,
  input  [15:0] EX_MEM_R,
  input  [1:0] MuxB_Slct,
  output [15:0] RD1_out,
  output [15:0] RD2_out
);

  Multiplexer #(.select(2), .width(16)) multiplexer_1 (
    .in0(ReadData1), .in1(ALUResult), .in2(EX_MEM_R), .out(RD1_out), .sel(MuxA_Slct));  // open: in3
  Multiplexer #(.select(2), .width(16)) multiplexer_2 (
    .in0(ReadData2), .in1(ALUResult), .in2(EX_MEM_R), .out(RD2_out), .sel(MuxB_Slct));  // open: in3

  // Notes on the sheet:
  //   MUXA
  //   MUXB
endmodule

module emux_slct (
  input  [2:0] IF_ID_Rs,
  input  [2:0] ID_EX_Rd,
  input  ID_EX_RegWrite,
  input  [2:0] EX_MEM_Rd,
  input  EX_MEM_RegWrite,
  input  [2:0] IF_ID_Rt,
  output [1:0] MuxA_Slct,
  output [1:0] MuxB_Slct
);

  wire and_2_out, and_4_out, comparator_1_eq, comparator_2_eq, comparator_3_eq, comparator_4_eq,
       comparator_5_eq, comparator_6_eq, comparator_7_eq, comparator_8_eq, not_1_out, not_2_out, not_3_out,
       not_4_out, not_5_out, not_6_out;

  Comparator #(.width(3)) comparator_1 (.a(IF_ID_Rs), .b(ID_EX_Rd), .eq(comparator_1_eq));  // open: gt, lt
  Comparator #(.width(3)) comparator_2 (.a(ID_EX_Rd), .b(3'b000), .eq(comparator_2_eq));  // open: gt, lt
  Comparator #(.width(3)) comparator_3 (.a(IF_ID_Rs), .b(EX_MEM_Rd), .eq(comparator_3_eq));  // open: gt, lt
  Comparator #(.width(3)) comparator_4 (.a(EX_MEM_Rd), .b(3'b000), .eq(comparator_4_eq));  // open: gt, lt
  Comparator #(.width(3)) comparator_5 (.a(IF_ID_Rt), .b(ID_EX_Rd), .eq(comparator_5_eq));  // open: gt, lt
  Comparator #(.width(3)) comparator_6 (.a(ID_EX_Rd), .b(3'b000), .eq(comparator_6_eq));  // open: gt, lt
  Comparator #(.width(3)) comparator_7 (.a(IF_ID_Rt), .b(EX_MEM_Rd), .eq(comparator_7_eq));  // open: gt, lt
  Comparator #(.width(3)) comparator_8 (.a(EX_MEM_Rd), .b(3'b000), .eq(comparator_8_eq));  // open: gt, lt
  not not_1 (not_1_out, comparator_2_eq);
  not not_2 (not_2_out, comparator_4_eq);
  not not_3 (not_3_out, comparator_6_eq);
  not not_4 (not_4_out, comparator_8_eq);
  and and_1 (MuxA_Slct[0], comparator_1_eq, ID_EX_RegWrite, not_1_out);
  not not_5 (not_5_out, MuxA_Slct[0]);
  and and_2 (and_2_out, comparator_3_eq, not_2_out, EX_MEM_RegWrite);
  and and_3 (MuxB_Slct[0], comparator_5_eq, ID_EX_RegWrite, not_3_out);
  not not_6 (not_6_out, MuxB_Slct[0]);
  and and_4 (and_4_out, comparator_7_eq, not_4_out, EX_MEM_RegWrite);
  and and_5 (MuxA_Slct[1], not_5_out, and_2_out);
  and and_6 (MuxB_Slct[1], not_6_out, and_4_out);
endmodule
